# Fritzing sketch PiezoServoUnoUSB (saved by Fritzing 0.9.2b)

parts:
  ArduinoUnoExt = Arduino Uno (Rev3)
  R1 = Resistor [resistance=1M tolerance=±5% package=THT]
  Servo = Basic Servo
  PiezoSensor = Piezo Speaker

nets:
  N1: ArduinoUnoExt.A2, R1.Pin_0, PiezoSensor.pin2
  GND: ArduinoUnoExt.GND, R1.Pin_1, Servo.gnd, PiezoSensor.pin1
  N2: ArduinoUnoExt.D7, Servo.pulse
  5V: ArduinoUnoExt.5V, Servo.vcc
